// Logisim project obvody.circ as structural Verilog: 25 circuits, main circuit f
module f (
  input  x,
  input  y,
  input  z,
  output f
);

  wire nand_1_out, nand_2_out, nand_3_out, nand_4_out, nand_5_out;

  nand nand_1 (nand_1_out, x, y);
  nand nand_2 (nand_2_out, y, z);
  nand nand_3 (nand_3_out, z, x);
  nand nand_4 (nand_4_out, nand_1_out, nand_2_out);
  nand nand_5 (nand_5_out, nand_4_out, nand_4_out);
  nand nand_6 (f, nand_5_out, nand_3_out);
endmodule

module komparator_1 (
  input  A,
  input  B,
  output Y,
  output Y_2,
  output Y_3
);

  wire nand_1_out, nand_2_out, nand_3_out, not_1_out, not_2_out;

  not not_1 (not_1_out, A);
  not not_2 (not_2_out, B);
  nand nand_1 (nand_1_out, A, not_2_out);
  nand nand_2 (nand_2_out, not_1_out, B);
  not not_3 (Y, nand_1_out);
  not not_4 (Y_2, nand_3_out);
  nand nand_3 (nand_3_out, nand_1_out, nand_2_out);
  not not_5 (Y_3, nand_2_out);
endmodule

// >=
module komparator_i (
  input  Ai,
  input  in_2,
  input  Bi,
  output out_4,
  output Yi,
  output out_6
);

  wire nand_3_out, not_1_out, not_2_out;

  not not_1 (not_1_out, Ai);
  not not_2 (not_2_out, Bi);
  nand nand_1 (out_4, Ai, not_2_out, in_2);
  nand nand_2 (out_6, in_2, not_1_out, Bi);
  nand nand_3 (nand_3_out, out_4, in_2, out_6);
  not not_3 (Yi, nand_3_out);
endmodule

module komparator_4 (
  input  A3,
  input  A2,
  input  A1,
  input  A0,
  input  B3,
  input  B2,
  input  B1,
  input  B0,
  output Y,
  output Y_2,
  output Y_3
);

  wire komparator_i_1_out_4, komparator_i_1_out_6, komparator_i_1_yi, komparator_i_2_out_4,
       komparator_i_2_out_6, komparator_i_2_yi, komparator_i_3_out_4, komparator_i_3_out_6,
       komparator_i_3_yi, komparator_i_4_out_4, komparator_i_4_out_6;

  komparator_i komparator_i_1 (
    .Ai(A3), .in_2(1'b1), .Bi(B3), .out_4(komparator_i_1_out_4), .Yi(komparator_i_1_yi),
    .out_6(komparator_i_1_out_6));
  komparator_i komparator_i_2 (
    .Ai(A2), .in_2(komparator_i_1_yi), .Bi(B2), .out_4(komparator_i_2_out_4), .Yi(komparator_i_2_yi),
    .out_6(komparator_i_2_out_6));
  komparator_i komparator_i_3 (
    .Ai(A1), .in_2(komparator_i_2_yi), .Bi(B1), .out_4(komparator_i_3_out_4), .Yi(komparator_i_3_yi),
    .out_6(komparator_i_3_out_6));
  komparator_i komparator_i_4 (
    .Ai(A0), .in_2(komparator_i_3_yi), .Bi(B0), .out_4(komparator_i_4_out_4), .Yi(Y_2),
    .out_6(komparator_i_4_out_6));
  nand nand_1 (Y, komparator_i_1_out_4, komparator_i_2_out_4, komparator_i_3_out_4, komparator_i_4_out_4);
  nand nand_2 (Y_3, komparator_i_4_out_6, komparator_i_3_out_6, komparator_i_2_out_6, komparator_i_1_out_6);
endmodule

module dekoder (
  input  A0,
  input  A1,
  output S0,
  output S1,
  output S2,
  output S3
);

  wire not_1_out, not_2_out;

  not not_1 (not_1_out, A0);
  not not_2 (not_2_out, A1);
  and and_1 (S0, not_1_out, not_2_out);
  and and_2 (S1, not_2_out, A0);
  and and_3 (S2, not_1_out, A1);
  and and_4 (S3, A0, A1);
endmodule

module multiplexor (
  input  A0,
  input  A1,
  input  D0,
  input  D1,
  input  D2,
  input  D3,
  output Q,
  output not_Q
);

  wire and_1_out, and_2_out, and_3_out, and_4_out, not_1_out, not_2_out;

  not not_1 (not_1_out, A0);
  not not_2 (not_2_out, A1);
  and and_1 (and_1_out, not_1_out, not_2_out, D0);
  and and_2 (and_2_out, A0, not_2_out, D1);
  and and_3 (and_3_out, not_1_out, A1, D2);
  and and_4 (and_4_out, A0, A1, D3);
  or or_1 (Q, and_1_out, and_2_out, and_3_out, and_4_out);
  not not_3 (not_Q, Q);
endmodule

module multiplexor_dekoder (
  input  A1,
  input  A0,
  input  D0,
  input  D1,
  input  D2,
  input  D3,
  output Q,
  output not_Q
);

  wire and_1_out, and_2_out, and_3_out, and_4_out, dekoder_1_s0, dekoder_1_s1, dekoder_1_s2, dekoder_1_s3;

  dekoder dekoder_1 (.A0(A0), .A1(A1), .S0(dekoder_1_s0), .S1(dekoder_1_s1), .S2(dekoder_1_s2), .S3(dekoder_1_s3));
  and and_1 (and_1_out, dekoder_1_s0, D0);
  and and_2 (and_2_out, dekoder_1_s1, D1);
  and and_3 (and_3_out, dekoder_1_s2, D2);
  and and_4 (and_4_out, dekoder_1_s3, D3);
  or or_1 (Q, and_1_out, and_2_out, and_3_out, and_4_out);
  not not_1 (not_Q, Q);
endmodule

module pul_scitacka (
  input  A,
  input  B,
  output S,
  output r
);

  xor xor_1 (S, A, B);
  and and_1 (r, B, A);
endmodule

module scitacka (
  input  ri_1,
  input  Ai,
  input  Bi,
  output Si,
  output ri
);

  wire and_1_out, and_2_out, xor_1_out;

  xor xor_1 (xor_1_out, Ai, Bi);
  and and_1 (and_1_out, Bi, Ai);
  xor xor_2 (Si, ri_1, xor_1_out);
  and and_2 (and_2_out, ri_1, xor_1_out);
  or or_1 (ri, and_2_out, and_1_out);
endmodule

module scitacka_4 (
  input  A0,
  input  A1,
  input  A2,
  input  A3,
  input  B0,
  input  B1,
  input  B2,
  input  B3,
  output S0,
  output S1,
  output S2,
  output S3,
  output r
);

  wire scitacka_1_ri, scitacka_2_ri, scitacka_3_ri;

  scitacka scitacka_1 (.ri_1(1'b0), .Ai(A0), .Bi(B0), .Si(S0), .ri(scitacka_1_ri));
  scitacka scitacka_2 (.ri_1(scitacka_1_ri), .Ai(A1), .Bi(B1), .Si(S1), .ri(scitacka_2_ri));
  scitacka scitacka_3 (.ri_1(scitacka_2_ri), .Ai(A2), .Bi(B2), .Si(S2), .ri(scitacka_3_ri));
  scitacka scitacka_4 (.ri_1(scitacka_3_ri), .Ai(A3), .Bi(B3), .Si(S3), .ri(r));
endmodule

module nasobicka_2 (
  input  B1,
  input  B0,
  input  A0,
  input  A1,
  output M3,
  output M2,
  output M1,
  output M0
);

  wire and_1_out, and_2_out, and_3_out, scitacka_2_ri;

  and and_1 (and_1_out, A1, B1);
  scitacka scitacka_1 (.ri_1(scitacka_2_ri), .Ai(and_1_out), .Bi(1'b0), .Si(M2), .ri(M3));
  and and_2 (and_2_out, A0, B1);
  and and_3 (and_3_out, A1, B0);
  and and_4 (M0, A0, B0);
  scitacka scitacka_2 (.ri_1(1'b0), .Ai(and_3_out), .Bi(and_2_out), .Si(M1), .ri(scitacka_2_ri));
endmodule

module nasobicka_4 (
  input  B3,
  input  B2,
  input  B1,
  input  B0,
  input  A0,
  input  A1,
  input  A2,
  input  A3,
  output M7,
  output M6,
  output M5,
  output M4,
  output M3,
  output M2,
  output M1,
  output M0
);

  wire and_1_out, and_2_out, and_3_out, and_4_out, and_5_out, and_6_out, and_7_out, and_8_out, and_9_out,
       and_10_out, and_11_out, and_12_out, and_13_out, and_14_out, and_15_out, scitacka_2_ri, scitacka_3_ri,
       scitacka_3_si, scitacka_4_ri, scitacka_4_si, scitacka_5_ri, scitacka_6_ri, scitacka_6_si,
       scitacka_7_ri, scitacka_7_si, scitacka_8_ri, scitacka_8_si, scitacka_9_ri, scitacka_10_ri,
       scitacka_10_si, scitacka_11_ri, scitacka_11_si, scitacka_12_ri, scitacka_12_si, scitacka_13_ri,
       scitacka_14_ri, scitacka_14_si, scitacka_15_ri, scitacka_15_si, scitacka_16_ri, scitacka_17_ri;

  scitacka scitacka_1 (.ri_1(1'b0), .Ai(scitacka_3_ri), .Bi(scitacka_2_ri), .Si(M7));  // open: ri
  and and_1 (and_1_out, A3, B3);
  scitacka scitacka_2 (.ri_1(scitacka_7_ri), .Ai(scitacka_3_si), .Bi(and_1_out), .Si(M6), .ri(scitacka_2_ri));
  and and_2 (and_2_out, A2, B3);
  scitacka scitacka_3 (.ri_1(scitacka_5_ri), .Ai(scitacka_4_ri), .Bi(1'b0), .Si(scitacka_3_si), .ri(scitacka_3_ri));
  and and_3 (and_3_out, A1, B3);
  and and_4 (and_4_out, A3, B2);
  scitacka scitacka_4 (
    .ri_1(scitacka_11_ri), .Ai(scitacka_7_si), .Bi(and_4_out), .Si(scitacka_4_si), .ri(scitacka_4_ri));
  scitacka scitacka_5 (.ri_1(1'b0), .Ai(scitacka_4_si), .Bi(and_2_out), .Si(M5), .ri(scitacka_5_ri));
  and and_5 (and_5_out, A2, B2);
  scitacka scitacka_6 (.ri_1(1'b0), .Ai(and_5_out), .Bi(and_3_out), .Si(scitacka_6_si), .ri(scitacka_6_ri));
  scitacka scitacka_7 (
    .ri_1(scitacka_9_ri), .Ai(scitacka_8_ri), .Bi(scitacka_6_ri), .Si(scitacka_7_si), .ri(scitacka_7_ri));
  and and_6 (and_6_out, A3, B1);
  scitacka scitacka_8 (
    .ri_1(scitacka_14_ri), .Ai(scitacka_11_si), .Bi(and_6_out), .Si(scitacka_8_si), .ri(scitacka_8_ri));
  scitacka scitacka_9 (.ri_1(1'b0), .Ai(scitacka_8_si), .Bi(scitacka_6_si), .Si(M4), .ri(scitacka_9_ri));
  and and_7 (and_7_out, A0, B3);
  and and_8 (and_8_out, A1, B2);
  and and_9 (and_9_out, A2, B1);
  scitacka scitacka_10 (.ri_1(1'b0), .Ai(and_8_out), .Bi(and_7_out), .Si(scitacka_10_si), .ri(scitacka_10_ri));
  scitacka scitacka_11 (
    .ri_1(scitacka_13_ri), .Ai(scitacka_12_ri), .Bi(scitacka_10_ri), .Si(scitacka_11_si), .ri(scitacka_11_ri));
  and and_10 (and_10_out, A3, B0);
  scitacka scitacka_12 (
    .ri_1(scitacka_14_si), .Ai(and_10_out), .Bi(and_9_out), .Si(scitacka_12_si), .ri(scitacka_12_ri));
  scitacka scitacka_13 (.ri_1(1'b0), .Ai(scitacka_12_si), .Bi(scitacka_10_si), .Si(M3), .ri(scitacka_13_ri));
  and and_11 (and_11_out, A0, B2);
  and and_12 (and_12_out, A1, B1);
  scitacka scitacka_14 (
    .ri_1(scitacka_16_ri), .Ai(scitacka_15_ri), .Bi(1'b0), .Si(scitacka_14_si), .ri(scitacka_14_ri));
  and and_13 (and_13_out, A2, B0);
  scitacka scitacka_15 (
    .ri_1(scitacka_17_ri), .Ai(and_13_out), .Bi(and_12_out), .Si(scitacka_15_si), .ri(scitacka_15_ri));
  scitacka scitacka_16 (.ri_1(1'b0), .Ai(scitacka_15_si), .Bi(and_11_out), .Si(M2), .ri(scitacka_16_ri));
  and and_14 (and_14_out, A0, B1);
  and and_15 (and_15_out, A1, B0);
  and and_16 (M0, A0, B0);
  scitacka scitacka_17 (.ri_1(1'b0), .Ai(and_15_out), .Bi(and_14_out), .Si(M1), .ri(scitacka_17_ri));
endmodule

// RS
module klopny_RS (
  input  S,
  input  R,
  output Q,
  output not_Q
);

  wire not_1_out, not_2_out;

  not not_1 (not_1_out, S);
  not not_2 (not_2_out, R);
  nand nand_1 (Q, not_1_out, not_Q);
  nand nand_2 (not_Q, Q, not_2_out);
endmodule

// RSC
module klopny_RSC_uroven (
  input  S,
  input  CLK,
  input  R,
  output Q,
  output not_Q
);

  wire and_1_out, and_2_out;

  and and_1 (and_1_out, S, CLK);
  and and_2 (and_2_out, CLK, R);
  klopny_RS klopny_rs_1 (.S(and_1_out), .R(and_2_out), .Q(Q), .not_Q(not_Q));
endmodule

// RSC
module klopny_RSC_hrana (
  input  S,
  input  CLK,
  input  R,
  output Q,
  output not_Q
);

  S_R_Flip_Flop s_r_ff_1 (.S(S), .clk(CLK), .R(R), .Q(Q), .Qn(not_Q));  // open: preset, reset, en
endmodule

// D
module klopny_D_uroven (
  input  D,
  input  CLK,
  output Q,
  output not_Q
);

  wire not_1_out;

  not not_1 (not_1_out, D);
  klopny_RSC_uroven klopny_rsc_uroven_1 (.S(D), .R(not_1_out), .Q(Q), .not_Q(not_Q), .CLK(CLK));
endmodule

// D
module klopny_D_hrana (
  input  D,
  input  CLK,
  output Q,
  output not_Q
);

  wire not_1_out;

  not not_1 (not_1_out, D);
  klopny_RSC_hrana klopny_rsc_hrana_1 (.S(D), .CLK(CLK), .R(not_1_out), .Q(Q), .not_Q(not_Q));
endmodule

// JK
module klopny_JK_uroven_RS (
  input  J,
  input  CLK,
  input  K,
  output Q,
  output not_Q
);

  wire and_1_out, and_2_out;

  and and_1 (and_1_out, not_Q, J, CLK);
  and and_2 (and_2_out, CLK, K, Q);
  klopny_RS klopny_rs_1 (.S(and_1_out), .R(and_2_out), .Q(Q), .not_Q(not_Q));
endmodule

// JK
module klopny_JK_uroven (
  input  J,
  input  CLK,
  input  K,
  output Q,
  output not_Q
);

  wire and_1_out, and_2_out;

  and and_1 (and_1_out, not_Q, J);
  and and_2 (and_2_out, K, Q);
  klopny_RSC_uroven klopny_rsc_uroven_1 (.S(and_1_out), .R(and_2_out), .Q(Q), .not_Q(not_Q), .CLK(CLK));
endmodule

// JK
module klopny_JK_hrana (
  input  J,
  input  CLK,
  input  K,
  output Q,
  output not_Q
);

  wire and_1_out, and_2_out;

  and and_1 (and_1_out, not_Q, J);
  and and_2 (and_2_out, K, Q);
  klopny_RSC_hrana klopny_rsc_hrana_1 (.S(and_1_out), .CLK(CLK), .R(and_2_out), .Q(Q), .not_Q(not_Q));
endmodule

module p_registr_4 (
  input  D0,
  input  D1,
  input  D2,
  input  D3,
  output Q0,
  output Q1,
  output Q2,
  output Q3
);

  wire clock_1_out;

  Clock clock_1 (.out(clock_1_out));
  klopny_D_uroven klopny_d_uroven_1 (.D(D0), .Q(Q0), .CLK(clock_1_out));  // open: not_Q
  klopny_D_uroven klopny_d_uroven_2 (.D(D1), .Q(Q1), .CLK(clock_1_out));  // open: not_Q
  klopny_D_uroven klopny_d_uroven_3 (.D(D2), .Q(Q2), .CLK(clock_1_out));  // open: not_Q
  klopny_D_uroven klopny_d_uroven_4 (.D(D3), .Q(Q3), .CLK(clock_1_out));  // open: not_Q
endmodule

module s_registr_4_uroven (
  input  D,
  output Q0,
  output Q1,
  output Q2,
  output Q3
);

  wire clock_1_out;

  Clock clock_1 (.out(clock_1_out));
  klopny_D_uroven klopny_d_uroven_1 (.D(D), .Q(Q0), .CLK(clock_1_out));  // open: not_Q
  klopny_D_uroven klopny_d_uroven_2 (.D(Q0), .Q(Q1), .CLK(clock_1_out));  // open: not_Q
  klopny_D_uroven klopny_d_uroven_3 (.D(Q1), .Q(Q2), .CLK(clock_1_out));  // open: not_Q
  klopny_D_uroven klopny_d_uroven_4 (.D(Q2), .Q(Q3), .CLK(clock_1_out));  // open: not_Q
endmodule

module s_registr_4_hrana (
  input  D,
  output Q0,
  output Q1,
  output Q2,
  output Q3
);

  wire clock_1_out;

  Clock clock_1 (.out(clock_1_out));
  klopny_D_hrana klopny_d_hrana_1 (.D(D), .Q(Q0), .CLK(clock_1_out));  // open: not_Q
  klopny_D_hrana klopny_d_hrana_2 (.D(Q0), .Q(Q1), .CLK(clock_1_out));  // open: not_Q
  klopny_D_hrana klopny_d_hrana_3 (.D(Q1), .Q(Q2), .CLK(clock_1_out));  // open: not_Q
  klopny_D_hrana klopny_d_hrana_4 (.D(Q2), .Q(Q3), .CLK(clock_1_out));  // open: not_Q
endmodule

module citac_4 (
  output Q0,
  output Q1,
  output Q2,
  output Q3
);

  wire clock_1_out, klopny_jk_hrana_1_q, klopny_jk_hrana_2_q, klopny_jk_hrana_3_q;

  Clock clock_1 (.out(clock_1_out));
  klopny_JK_hrana klopny_jk_hrana_1 (.J(1'b1), .Q(klopny_jk_hrana_1_q), .K(1'b1), .not_Q(Q0), .CLK(clock_1_out));
  klopny_JK_hrana klopny_jk_hrana_2 (
    .J(1'b1), .Q(klopny_jk_hrana_2_q), .K(1'b1), .not_Q(Q1), .CLK(klopny_jk_hrana_1_q));
  klopny_JK_hrana klopny_jk_hrana_3 (
    .J(1'b1), .Q(klopny_jk_hrana_3_q), .K(1'b1), .not_Q(Q2), .CLK(klopny_jk_hrana_2_q));
  klopny_JK_hrana klopny_jk_hrana_4 (.J(1'b1), .K(1'b1), .not_Q(Q3), .CLK(klopny_jk_hrana_3_q));  // open: Q
endmodule

module pamet_4_2 (
  input  In0,
  input  In1,
  input  A0,
  input  write,
  input  A1,
  output Out0,
  output Out1
);

  wire and_1_out, and_2_out, and_3_out, and_4_out, and_5_out, and_6_out, and_7_out, and_8_out, and_9_out,
       and_10_out, and_11_out, and_12_out, and_13_out, clock_1_out, dekoder_1_s0, dekoder_1_s1, dekoder_1_s2,
       dekoder_1_s3, klopny_d_uroven_1_q, klopny_d_uroven_2_q, klopny_d_uroven_3_q, klopny_d_uroven_4_q,
       klopny_d_uroven_5_q, klopny_d_uroven_6_q, klopny_d_uroven_7_q, klopny_d_uroven_8_q;

  and and_1 (and_1_out, clock_1_out, write);
  Clock clock_1 (.out(clock_1_out));
  klopny_D_uroven klopny_d_uroven_1 (.D(In0), .Q(klopny_d_uroven_1_q), .CLK(and_2_out));  // open: not_Q
  klopny_D_uroven klopny_d_uroven_2 (.D(In1), .Q(klopny_d_uroven_2_q), .CLK(and_2_out));  // open: not_Q
  and and_2 (and_2_out, and_1_out, dekoder_1_s0);
  and and_3 (and_3_out, klopny_d_uroven_1_q, dekoder_1_s0);
  and and_4 (and_4_out, klopny_d_uroven_2_q, dekoder_1_s0);
  klopny_D_uroven klopny_d_uroven_3 (.D(In0), .Q(klopny_d_uroven_3_q), .CLK(and_5_out));  // open: not_Q
  klopny_D_uroven klopny_d_uroven_4 (.D(In1), .Q(klopny_d_uroven_4_q), .CLK(and_5_out));  // open: not_Q
  and and_5 (and_5_out, and_1_out, dekoder_1_s1);
  dekoder dekoder_1 (.A0(A0), .A1(A1), .S0(dekoder_1_s0), .S1(dekoder_1_s1), .S2(dekoder_1_s2), .S3(dekoder_1_s3));
  and and_6 (and_6_out, klopny_d_uroven_3_q, dekoder_1_s1);
  and and_7 (and_7_out, klopny_d_uroven_4_q, dekoder_1_s1);
  and and_8 (and_8_out, and_1_out, dekoder_1_s2);
  klopny_D_uroven klopny_d_uroven_5 (.D(In0), .Q(klopny_d_uroven_5_q), .CLK(and_8_out));  // open: not_Q
  klopny_D_uroven klopny_d_uroven_6 (.D(In1), .Q(klopny_d_uroven_6_q), .CLK(and_8_out));  // open: not_Q
  and and_9 (and_9_out, klopny_d_uroven_5_q, dekoder_1_s2);
  and and_10 (and_10_out, klopny_d_uroven_6_q, dekoder_1_s2);
  and and_11 (and_11_out, and_1_out, dekoder_1_s3);
  klopny_D_uroven klopny_d_uroven_7 (.D(In0), .Q(klopny_d_uroven_7_q), .CLK(and_11_out));  // open: not_Q
  klopny_D_uroven klopny_d_uroven_8 (.D(In1), .Q(klopny_d_uroven_8_q), .CLK(and_11_out));  // open: not_Q
  and and_12 (and_12_out, klopny_d_uroven_7_q, dekoder_1_s3);
  and and_13 (and_13_out, klopny_d_uroven_8_q, dekoder_1_s3);
  or or_1 (Out0, and_3_out, and_6_out, and_9_out, and_12_out);
  or or_2 (Out1, and_4_out, and_7_out, and_10_out, and_13_out);
endmodule
